// Logisim project add1b.circ as structural Verilog: 1 circuit, main circuit main
module main (
  input  a,
  input  b,
  output S__sortie,
  output R__retnue
);

  xor xor_1 (S__sortie, a, b);
  and and_1 (R__retnue, a, b);
endmodule
