// Logisim project add1complet.circ as structural Verilog: 1 circuit, main circuit main
module main (
  input  a,
  input  b,
  input  c,
  output S__sortie,
  output R__retenue
);

  wire and_1_out, and_2_out, and_3_out, xor_1_out;

  xor xor_1 (xor_1_out, a, b);
  and and_1 (and_1_out, a, b);
  and and_2 (and_2_out, a, c);
  and and_3 (and_3_out, b, c);
  xor xor_2 (S__sortie, xor_1_out, c);
  or or_1 (R__retenue, and_1_out, and_2_out, and_3_out);
endmodule
