// Logisim project add4b.circ as structural Verilog: 1 circuit, main circuit main
module main (
  input  b0,
  input  b1,
  input  b2,
  input  b3,
  input  a0,
  input  a1,
  input  a2,
  input  a3,
  output S0,
  output S1,
  output S2,
  output S3
);

  Adder #(.width(1)) adder_1 (.a(b0), .b(a0), .out(S0));  // open: cin, cout
  Adder #(.width(1)) adder_2 ();  // open: a, b, out, cin, cout
  Adder #(.width(1)) adder_3 ();  // open: a, b, out, cin, cout
  Adder #(.width(1)) adder_4 ();  // open: a, b, out, cin, cout
endmodule
