// Logisim project add4b_corr.circ as structural Verilog: 1 circuit, main circuit main
module main (
  input  b0,
  input  b1,
  input  b2,
  input  b3,
  input  a0,
  input  a1,
  input  a2,
  input  a3,
  output S0,
  output S1,
  output S2,
  output S3
);

  wire adder_1_cout, adder_2_cout, adder_3_cout;

  Adder #(.width(1)) adder_1 (.a(b0), .b(a0), .out(S0), .cout(adder_1_cout));  // open: cin
  Adder #(.width(1)) adder_2 (.a(b1), .b(a1), .out(S1), .cin(adder_1_cout), .cout(adder_2_cout));
  Adder #(.width(1)) adder_3 (.a(b2), .b(a2), .out(S2), .cin(adder_2_cout), .cout(adder_3_cout));
  Adder #(.width(1)) adder_4 (.a(b3), .b(a3), .out(S3), .cin(adder_3_cout));  // open: cout
endmodule
