// Logisim project Correction add 2 bits.circ as structural Verilog: 1 circuit, main circuit main
module main (
  input  a,
  input  b,
  input  in_3,
  input  a_2,
  input  b_2,
  input  a1,
  input  a0,
  input  b0,
  input  b1,
  output R,
  output out_11,
  output S,
  output out_13,
  output S_2,
  output R_2,
  output S0,
  output S1,
  output out_18
);

  wire adder_2_cout, not_1_out, not_2_out;

  not not_1 (not_1_out, b);
  not not_2 (not_2_out, a);
  and and_1 (out_11, a, not_1_out);
  and and_2 (out_13, not_2_out, b);
  Adder #(.width(1)) adder_1 (.a(a_2), .b(b_2), .out(S_2), .cin(in_3), .cout(R_2));
  Adder #(.width(1)) adder_2 (.a(a0), .b(b0), .out(S0), .cout(adder_2_cout));  // open: cin
  and and_3 (R, a, b);
  Adder #(.width(1)) adder_3 (.a(a1), .b(b1), .out(S1), .cin(adder_2_cout), .cout(out_18));
  or or_1 (S, out_11, out_13);
endmodule
