// Logisim project UAL.circ as structural Verilog: 1 circuit, main circuit main
module main (
  input  [3:0] a,
  input  [3:0] b,
  input  [3:0] opcode,
  output [3:0] out_4,
  output [3:0] ADD,
  output [3:0] MUX,
  output Overflow,
  output [3:0] out_8,
  output [3:0] NAND,
  output [3:0] out_10
);

  wire not_1_out, not_2_out, not_3_out;

  assign out_4 = not_1_out ? a : 4'bz;  // Controlled_Buffer controlled_buffer_1
  assign out_10 = not_2_out ? b : 4'bz;  // Controlled_Buffer controlled_buffer_2
  assign out_4 = opcode[3] ? ~a : 4'bz;  // Controlled_Inverter controlled_inverter_1
  not not_1 (not_1_out, opcode[3]);
  assign out_10 = opcode[2] ? ~b : 4'bz;  // Controlled_Inverter controlled_inverter_2
  not not_2 (not_2_out, opcode[2]);
  Adder #(.width(4)) adder_1 (.a(out_4), .b(out_10), .out(ADD), .cout(Overflow));  // open: cin
  assign NAND = ~(out_4 & out_10);  // NAND_Gate nand_1, 4 bits wide
  Multiplexer #(.width(4), .enable("false")) multiplexer_1 (.in0(ADD), .in1(NAND), .out(MUX), .sel(opcode[1]));
  assign out_8 = not_3_out ? MUX : 4'bz;  // Controlled_Buffer controlled_buffer_3
  assign out_8 = opcode[0] ? ~MUX : 4'bz;  // Controlled_Inverter controlled_inverter_3
  not not_3 (not_3_out, opcode[0]);

  // Notes on the sheet:
  //   INV
  //   INV
  //   INV
  //   OUT
endmodule
