// Logisim project additionneur 1 bits.circ as structural Verilog: 1 circuit, main circuit main
module main (
  input  in_1,
  input  in_2,
  input  in_3,
  input  in_4,
  input  in_5,
  output out_6,
  output out_7,
  output S,
  output out_9
);

  wire and_1_out, and_2_out, not_1_out, not_2_out;

  not not_1 (not_1_out, in_4);
  not not_2 (not_2_out, in_5);
  Adder #(.width(1)) adder_1 (.a(in_2), .b(in_3), .out(out_6), .cin(in_1), .cout(out_7));
  and and_1 (and_1_out, in_5, not_1_out);
  and and_2 (and_2_out, in_4, not_2_out);
  and and_3 (out_9, in_4, in_5);
  or or_1 (S, and_1_out, and_2_out);
endmodule
