// Logisim project additionneur 4 bits.circ as structural Verilog: 1 circuit, main circuit main
module main (
  input  in_1,
  input  in_2,
  input  in_3,
  input  in_4,
  input  in_5,
  input  in_6,
  input  in_7,
  input  in_8,
  input  in_9,
  output out_10,
  output out_11,
  output out_12,
  output out_13,
  output out_14
);

  wire adder_1_cout, adder_2_cout, adder_3_cout;

  Adder #(.width(1)) adder_1 (.a(in_4), .b(in_6), .out(out_10), .cin(in_5), .cout(adder_1_cout));
  Adder #(.width(1)) adder_2 (.a(in_3), .b(in_7), .out(out_11), .cin(adder_1_cout), .cout(adder_2_cout));
  Adder #(.width(1)) adder_3 (.a(in_2), .b(in_8), .out(out_12), .cin(adder_2_cout), .cout(adder_3_cout));
  Adder #(.width(1)) adder_4 (.a(in_1), .b(in_9), .out(out_13), .cin(adder_3_cout), .cout(out_14));
endmodule
