// Logisim project efface.circ as structural Verilog: 1 circuit, main circuit main
module main (
  input  in_1,
  input  in_2,
  output S,
  output out_4
);

  wire and_1_out, and_2_out, not_1_out, not_2_out;

  not not_1 (not_1_out, in_1);
  not not_2 (not_2_out, in_2);
  and and_1 (and_1_out, in_2, not_1_out);
  and and_2 (and_2_out, in_1, not_2_out);
  and and_3 (out_4, in_1, in_2);
  Adder #(.width(1)) adder_1 ();  // open: a, b, out, cin, cout
  or or_1 (S, and_1_out, and_2_out);
  Adder #(.width(1)) adder_2 ();  // open: a, b, out, cin, cout
endmodule
